# Fritzing sketch vesta (saved by Fritzing 0.9.4)
breadboards: 2

parts:
  Raspberry_Pi_1 = Raspberry Pi 3 [part_number=RPI-3-V1.2]
  Part1 = Adafruit SGP30 Gas Sensor
  SparkFun_Ambient_Light_Sensor_-_VEML6030_(Qwiic)1 = SparkFun Ambient Light Sensor - VEML6030 (Qwiic) [part_number=SEN-15436]  # not connected
  Part2 = Adafruit BME280
  DHT1 = DHT22 Humidity and Temperature Sensor
  U1 = LCD-16X2 [package=lcd-16x2_noholes]  # not connected
  R1 = Trimmer Potentiometer [maximum_resistance=10kΩ package=THT]
  R2 = Trimmer Potentiometer [maximum_resistance=10kΩ package=THT]

nets:
  VIN: Raspberry_Pi_1.3v3, Part1.VIN, Part2.VIN, DHT1.VDD
  N1: Raspberry_Pi_1.GPIO2, Part1.SDA
  N2: Raspberry_Pi_1.GPIO3, Part1.SCL
  N3: Raspberry_Pi_1.GPIO4, DHT1.NULL
  GND: Raspberry_Pi_1.GND, Part1.GND, Part2.GND, DHT1.GND, R1.leg2, R2.leg2
  N4: Raspberry_Pi_1.GPIO10, Part2.SDI/SDA
  N5: Raspberry_Pi_1.GPIO9, Part2.SDO/ADR
  N6: Raspberry_Pi_1.GPIO11, Part2.SCK/SCL
  N7: Raspberry_Pi_1.GPIO7, Part2.CS
  N8: Raspberry_Pi_1.5V, R1.leg1, R2.leg1

custom parts:
  SparkFun Ambient Light Sensor - VEML6030 (Qwiic): Looking for an option to sense ambient light? The VEML6030 Qwiic board is a great starter option. The VEML6030 is a high accuracy ambient light sensor with 16-bit resolution. Even more impressive is that it can detect light similar to the human eye response. Utilizing our handy Qwiic system, no soldering is required to connect it to the rest of your system. However, we still have broken out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
  Adafruit BME280: Bosch has stepped up their game with their new BME280 sensor, an environmental sensor with temperature, barometric pressure and humidity! This sensor is great for all sorts of weather/environmental sensing and can even be used in both I2C and SPI! This precision sensor from Bosch is the best low-cost sensing solution for measuring humidity with ±3% accuracy, barometric pressure with ±1 hPa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
